# Fritzing sketch OutdoorStation (saved by Fritzing 0.9.3b)
breadboards: 1

parts:
  Part1 = Arduino Pro Mini v13
  Part2 = NRF24L01+ Breakout Board
  R1 = PHOTOCELL [package=photocell-kit]
  VCC1 = Battery
  R2 = Resistor [tolerance=±5% resistance=4.7k package=THT]
  Part3 = Adafruit BME280

nets:
  N1: Part1.A4, Part3.SDO/ADR
  N2: Part1.A5, Part3.SCK/SCL
  GND: Part1.GND, Part2.GND, VCC1.-, R2.Pin_1, Part3.GND
  VCC: Part1.VCC, Part2.VCC, R1.P$1, VCC1.+, Part3.3.3V
  N3: Part1.A0, R1.P$2, R2.Pin_0
  N4: Part1.D13/SCK, Part2.SCK
  N5: Part1.D12/MISO, Part2.MISO
  N6: Part1.D11_PWM/MOSI, Part2.MOSI
  N7: Part1.D10_PWM/SS, Part2.CS
  N8: Part1.D9_PWM, Part2.CE

custom parts:
  Adafruit BME280: Bosch has stepped up their game with their new BME280 sensor, an environmental sensor with temperature, barometric pressure and humidity! This sensor is great for all sorts of weather/environmental sensing and can even be used in both I2C and SPI! This precision sensor from Bosch is the best low-cost sensing solution for measuring humidity with ±3% accuracy, barometric pressure with ±1 hPa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
